# Fritzing sketch pushup-counter (saved by Fritzing 0.9.2b)
breadboards: 1

parts:
  Součástka1 = Arduino Nano (Rev3.0)
  Nokia_5110_LCD_Module1 = Nokia5110LCDModule
  J1 = Piezo Speaker
  LED1 = RGB LED (com. anode, rbg) [package="5 mm [THT]"]
  Součástka2 = HC-SR04 Ultrasonic Rangemeter
  R1 = Resistor [tolerance=±5% resistance=220 package=THT]
  Součástka3 = Four touch buttons

nets:
  GND: Součástka1.GND, Nokia_5110_LCD_Module1.LED, J1.pin1, LED1.common_anode, Součástka2.GND, Součástka3.GND
  N1: Součástka1.D2, Součástka2.Echo
  N2: Součástka1.D3, Součástka2.Trig
  N3: Součástka1.D4, Nokia_5110_LCD_Module1.Grnd
  N4: Součástka1.D5, Nokia_5110_LCD_Module1.SCE
  N5: Součástka1.D6, Nokia_5110_LCD_Module1.RST
  N6: Součástka1.D7, Nokia_5110_LCD_Module1.D/C
  N7: Součástka1.D9, J1.pin2, R1.Pin_0
  N8: Součástka1.D10, Nokia_5110_LCD_Module1.Vcc
  VCC: Součástka1.5V, Součástka2.VCC, Součástka3.VCC
  N9: Součástka1.A5, Součástka3.OUT1
  N10: Součástka1.A4, Součástka3.OUT2
  N11: Součástka1.A3, Součástka3.OUT3
  N12: Součástka1.A2, Součástka3.OUT4
  N13: Součástka1.3V3, Nokia_5110_LCD_Module1.6_DN_(MOSI), Nokia_5110_LCD_Module1.SCLK
  N14: LED1.blue_cathode, R1.Pin_1

custom parts:
  : Nokia 5110 LCD with 8 pin. It's a 45mm*45mm module part. Description: The Nokia 5110 is a basic graphic LCD screen for lots of applications. It was originally intended for as a cell phone screen. This one is mounted on an easy to solder PCB. It uses the PCD8544 controller. The PCD8544 is a low power CMOS LCD controller/driver, designed to drive a graphic display of 48 rows and 84 columns. All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
  Four touch buttons: todo
